# Fritzing sketch IR Sensor Sketch 2 (saved by Fritzing 0.9.3b)

parts:
  M1 = fc-51 [package=THT]
  Part1 = Arduino Nano (Rev3.0)
  M2 = 1 chan 5v relay module

nets:
  N1: M1.pin1, Part1.D2
  N2: M1.pin2, Part1.GND, M2.pin_2
  N3: M1.pin3, Part1.5V, M2.pin_1
  N4: Part1.D3, M2.pin_3

custom parts:
  1 chan 5v relay module: 1 Channel 5V Relay Module Board Shield with Optocoupler Support High and Low Level Trigger for Arduino.
